// Digital circuit CPU_main.dig as structural Verilog
module CPU_main (
  input  clk
);

  wire Acc_in, Acc_out, ALU_out, B_reg_in, CLR_T, IR_in, IR_out, MAR_in, MEM_out, PC_enable, PC_load, PC_out,
       RESET, START;
  wire [2:0] ALU_Op, COUNTER;
  wire [3:0] ADRESS, OPCODE;
  wire [7:0] Acc_q, alu_main_1_s_out, B_reg_q, MAR_q, PC_out_2, W_BUS;
  wire [15:0] CONTROL_ROM_d;

  Button u_RESET (.out(RESET));
  // Probe on RESET
  // Probe on clk
  // Probe on COUNTER
  // Probe on OPCODE
  CounterPreset #(.Bits(8)) PC (
    .en(PC_enable), .C(clk), .dir(1'b0), .in(W_BUS), .ld(PC_load), .clr(RESET), .out(PC_out_2));  // open: ovf
  // Probe on {OPCODE, COUNTER}
  assign W_BUS = PC_out ? PC_out_2 : 8'bz;  // Driver driver_1
  // Probe PC_PROBE on PC_out_2
  ROM #(.AddrBits(7), .Bits(16)) CONTROL_ROM (.A({OPCODE, COUNTER}), .sel(1'b1), .D(CONTROL_ROM_d));
  Counter #(.Bits(3)) u_Counter (.en(1'b1), .C(clk), .clr(CLR_T), .out(COUNTER));  // open: ovf
  // Probe on CONTROL_ROM_d
  Register #(.Bits(16)) Micro (
    .D(CONTROL_ROM_d), .C(clk), .en(1'b1),
    .Q({ALU_Op, PC_out, MAR_in, MEM_out, IR_in, IR_out, Acc_in, Acc_out, ALU_out, B_reg_in, PC_enable, PC_load, CLR_T, START}));
  // Probe on COUNTER
  Register #(.Bits(8)) IR (.D(W_BUS), .C(clk), .en(IR_in), .Q({ADRESS, OPCODE}));
  assign W_BUS = IR_out ? {ADRESS, OPCODE} : 8'bz;  // Driver driver_2
  // Probe IR_PROBE on {ADRESS, OPCODE}
  // Probe on IR_in
  Register #(.Bits(8)) B_reg (.D(W_BUS), .C(clk), .en(B_reg_in), .Q(B_reg_q));
  Register #(.Bits(8)) Acc (.D(W_BUS), .C(clk), .en(Acc_in), .Q(Acc_q));
  assign W_BUS = Acc_out ? Acc_q : 8'bz;  // Driver driver_3
  // Probe ACC_PROBE on Acc_q
  ALU_main alu_main_1 (
    .A_in(Acc_q), .B_in(B_reg_q), .ALU_op(ALU_Op), .CLK(clk), .START(START), .S_out(alu_main_1_s_out));  // open: Z_flag, ALU_busy
  assign W_BUS = ALU_out ? alu_main_1_s_out : 8'bz;  // Driver driver_4
  Register #(.Bits(8)) MAR (.D(W_BUS), .C(clk), .en(MAR_in), .Q(MAR_q));
  // Probe MAR_PROBE on MAR_q
  ROM #(.AddrBits(8), .Bits(8)) ROM (.A(MAR_q), .sel(MEM_out), .D(W_BUS));

  // Notes on the sheet:
  //   contents of CONTROL_ROM (hex, n*v repeats v):
  //   1800,8,600,900,480,2,10*0,900,410,a0,2
  //   contents of ROM (hex, n*v repeats v):
  //   e,1f,12*0,a,5
endmodule
